# Fritzing sketch node01_FrontDoor (saved by Fritzing 0.9.3b)
perfboards: 1

parts:
  PIR1 = PIR sensor [part_number=S3]
  S1 = SWITCH-MOMENTARY-2 [part_number=S4 package=reed_switch_pth]
  KY-1 = Keyes Relay [part_number=A1 package=THT]
  Part5 = NRF24L01+ Breakout Board
  Part6 = Arduino Nano (Rev3.0)
  J7 = screw terminal, 3 pins
  M1 = Stepper Motor - Bipolar
  Power_plug1 = Power plug
  S3 = SWITCH-SPST-2 [package=switch-spst-vertical]

nets:
  VDD: PIR1.VDD, KY-1.power, Part6.VIN, J7.pin3, Power_plug1.VCC
  N1: PIR1.SIG, Part6.D5, S3.P
  GND: PIR1.GND, S1.1, KY-1.ground, Part5.GND, Part6.GND, J7.pin1, Power_plug1.GND
  N2: S1.2, Part6.D6
  N3: KY-1.signal, Part6.D2
  VCC: Part5.VCC, Part6.3V3
  N4: Part5.CE, Part6.D9
  N5: Part5.CS, Part6.D10
  N6: Part5.SCK, Part6.D13/SCK
  N7: Part5.MOSI, Part6.D11/MOSI
  N8: Part5.MISO, Part6.D12/MISO
  N9: Part6.D3, M1.B
  N10: Part6.D4, M1.C
  N11: Part6.5V, S3.O

notes:
  node 01 - Front Door

custom parts:
  Keyes Relay: The Keyes 5V relay module is suitable for SCM development, home appliance control. It uses a 5V~12V TIL control signal which can control DC / AC signal.

// code stored in the sketch: _1_FrontDoor.ino

#define SN "Front Door"                 // short Sketch name
#define SV "0.2"                        // short Sketch version
#define MY_NODE_ID 1                    // (1-254) to manually set Node ID

/* Includes
=========1=========2=========3=========4=========5=========6=========7========*/
#include "NRF24L01.h"                   // NRF24L01 definitions
#include <MySensors.h>                  // MySensors library
#include "zzz.h"                        // Explanation and inital variables

#include "a0.h"                         // Relay, to switch on the lights when needed
#include "a1.h"                         // Lock and unlock the front door

#include "s0.h"                         // PIR switch, check if someone is in front of the door
#include "s1.h"                         // Reed switch, check if door is open or closed
#include "s2.h"                         // Photovoltaic sensor, to check if it's dark

/* Presentation
=========1=========2=========3=========4=========5=========6=========7========*/
void presentation(){ 
    sendSketchInfo(SN, SV);             // Send the sketch version information
    // Register the sensor(s) to the controller
    /* void present(uint8_t childSensorId, uint8_t sensorType, const char *description, bool ack); */
    present(0, S_MOTION, "PIR switch");
    present(1, S_DOOR, "Reed switch");
    present(2, S_LIGHT_LEVEL, "PV switch");
    present(3, S_BINARY, "Lights relay");
    //Serial.println("=== Node presented === ");
}

/* Setup
=========1=========2=========3=========4=========5=========6=========7========*/
void setup() {
    setup_s0();
    setup_s1();
    setup_s2();
    setup_a0();
    //Serial.println( "=== Node setup done ===" );
}

/* Loop
=========1=========2=========3=========4=========5=========6=========7========*/
void loop() {
    loop_s0();
    loop_s1();
    loop_s2();
    wait(1000);                         // wait a bit, loop once per second
}

/* Receive
=========1=========2=========3=========4=========5=========6=========7========*/
void receive(const MyMessage &message) {
    receive_a0(message);
}

// code stored in the sketch: _3_Patio.ino
#define SN "Patio"                      // short Sketch (Node) name
#define SV "1.1"                        // short Sketch (Node) version
#define MY_NODE_ID 1                    // (1-254) to manually set Node ID

/* Includes
=========1=========2=========3=========4=========5=========6=========7========*/
#include "NRF24L01.h"                   // NRF24L01 definitions
#include <MySensors.h>                  // MySensors library
#include "s1.h"                         // DHT11 for Temperature and Humidity
#include "a1.h"                         // Relay for Spotlight

/* Presentation
=========1=========2=========3=========4=========5=========6=========7========*/
void presentation(){ 
    sendSketchInfo(SN, SV);             // Send the sketch version information
    // Register sensor(s) to gateway    // void present(uint8_t childSensorId, uint8_t sensorType, const char *description, bool ack);
    present(0, S_HUM,"Patio Humidity");             // present sensor to gateway
    present(1, S_TEMP,"Patio Temperature");         // present sensor to gateway
    present(2, S_BINARY,"Patio Spotlight");         // present sensor to gateway
    metric = getConfig().isMetric;                  // ???
    //Serial.println("=== Node presented === ");    // Debug
}

/* Setup
=========1=========2=========3=========4=========5=========6=========7========*/
void setup(){
    setup_a1();
    setup_s1();
    //Serial.println( "=== Node setup done ===" ); // Debug
}

/* Loop
=========1=========2=========3=========4=========5=========6=========7========*/
void loop(){
    loop_s1();
}

/* Receive
=========1=========2=========3=========4=========5=========6=========7========*/
void receive(const MyMessage &message) {
    receive_a1(message);
    //Serial.println("=== Node message received === "); // Debug
}

// code stored in the sketch: a0.h
/* Single Relay actuator for door lights
=========1=========2=========3=========4=========5=========6=========7========*/
MyMessage msg_a0(3, V_STATUS);          // define type of message sent to MySensors

/* Setup
=========1=========2=========3=========4=========5=========6=========7========*/
void setup_a0(){
    pinMode(relayPin, OUTPUT);         // set pin to output mode
}

/* Receive
=========1=========2=========3=========4=========5=========6=========7========*/
void receive_a0(const MyMessage &message){
    if (message.type==V_LIGHT) {       // We only expect one type of message from controller.
        digitalWrite(relayPin, message.getBool() ? 1 : 0);  // Toggle relay state
        // Serial.print("Toggle relay. New state is "); Serial.println(message.getBool());
   } 
}

/* ON
=========1=========2=========3=========4=========5=========6=========7========*/
void lightsOn(){
    if (pvState < 500) {               // only switch on if PV sensor says it's dark
        digitalWrite(relayPin, 1);     // switch off 
    }
}

/* OFF
=========1=========2=========3=========4=========5=========6=========7========*/
void lightsOff(int t){
    wait(t * 60 * 1000);               // wait for t minutes
    digitalWrite(relayPin, 0);         // then switch off 
}

// code stored in the sketch: a0.h.ino
/* Single Relay actuator
=========1=========2=========3=========4=========5=========6=========7========*/
const int relayPin = 3;                 // define switch pin
MyMessage msgRel(3, V_STATUS);          // define type of message sent to MySensors

/* Setup
=========1=========2=========3=========4=========5=========6=========7========*/
void setup_s3(){
    pinMode(3, OUTPUT);                     // set pin 3 in output mode
    /*digitalWrite(relayPin, loadState(3) ? 1 : 0);  // Set relay to last known state (using eeprom storage) */
}

/* Receive
=========1=========2=========3=========4=========5=========6=========7========*/
void receive_s3(const MyMessage &message){
    if (message.type==V_LIGHT) {                           // We only expect one type of message from controller.
        digitalWrite(relayPin, message.getBool() ? 1 : 0);  // Toggle relay state
        /*saveState(3, message.getBool());                // Store state in eeprom*/
        // Serial.print("Toggle relay. New state is "); Serial.println(message.getBool());
   } 
}

// code stored in the sketch: A1.h
/*
    Single Relay
*/

/* Initialize
=========1=========2=========3=========4=========5=========6=========7========*/
MyMessage msgA1(A1, V_STATUS);


/* Setup
=========1=========2=========3=========4=========5=========6=========7========*/
void setupA1(){
    pinMode(pinA1, OUTPUT);             		// set relay pin in output mode
	digitalWrite(pinA1, loadState(A1)); 		// load state from eeprom
}


/* Receive
=========1=========2=========3=========4=========5=========6=========7========*/
void receiveA1(const MyMessage &message){
    if (message.type==V_STATUS) {
		digitalWrite(pinA1, message.getBool()); // toggle relay state
		saveState(A1,message.getBool());		// save state to eeprom
		Serial.println((String)"Toggle relay. New state is "+message.getBool());
	}
}

// code stored in the sketch: A2.h
/*
    Electronic Deadbolt control
	
	- setting A low and B high will operate the lock's motor in one direction
	  setting B low and A hight will operate the motor in the opposite direction
	- the power to both needs to cut off after x seconds, leaving them both low
	- I really just need to unlock, as it should lock itself in 30 seconds
	- how to get the status ?
	- Needs an H bridge circuit, like for remote controlled cars ?
	- RFID card some day ?
	- will 5V be enough to operate ?
*/

/* Initialize
=========1=========2=========3=========4=========5=========6=========7========*/
MyMessage msgA2(A2, V_LOCK_STATUS);			// type of message sent to MySensors

/* Setup
=========1=========2=========3=========4=========5=========6=========7========*/
void setupA2(){
	pinMode(pinA2L, OUTPUT);							// set pin to output mode
	pinMode(pinA2U, OUTPUT);		 					// set pin to output mode
}

/* Receive
=========1=========2=========3=========4=========5=========6=========7========*/
void receiveA2(const MyMessage &message){
	if (message.type==V_LOCK_STATUS) {
        //Serial.print("Received message: "); Serial.println(message.getInt());
		if (message.getInt() == 1){
            Serial.println("Lock Requested");
            digitalWrite(pinA2L, HIGH);
            digitalWrite(pinA2U, LOW);
            delay(1000);
            digitalWrite(pinA2L, LOW);
		} else if (message.getInt() == 0){
            Serial.println("Unlock Requested");
            digitalWrite(pinA2U, HIGH);
            digitalWrite(pinA2L, LOW);
            delay(1000);
            digitalWrite(pinA2U, LOW);
        }
    }
}

// code stored in the sketch: def.h

/*  SENSORS
=========1=========2=========3=========4=========5=========6=========7========*/
#define A1              1               // Relay for lights
#define A2              2               // Electric Door Lock
#define S1              3               // Reed switch
#define S4              4               // PIR switch 


/*  PINS & VARIABLES
=========1=========2=========3=========4=========5=========6=========7========*/

// A1 - Relay for lights
// ---------------------
const int pinA1 =       2;              // data pin
const int nightLight =  1;           	// a light that only works at night

// A2 - Lock/Unlock front door via electrick lock
// ----------------------------------------------
const int pinA2L =      3;          	// pin that locks the door
const int pinA2U =    	4;         		// pin that unlocks the door


/*       SENSORS
=========1=========2=========3=========4=========5=========6=========7========*/

// S1 - Reed switch - to sense if the door is open or closed
// ---------------------------------------------------------
const int pinS1 =       5;              // data pin with pull-up resistor
int valueS1 = 0;                        // reading the sensor status
int stateS1 = 0;                        // storing the last state

// S4 - PIR switch - to check if someone is in front of the door
// -------------------------------------------------------------
const int pinS4 =       6;              // data pin
bool valueS4 = 0;                       // reading the sensor status
bool stateS4 = 0;                       // storing the last state
unsigned long tS4;                      // store time of last trigger

// code stored in the sketch: node01_FrontDoor.ino
#define SN "Front Door"                 // short Sketch name
#define SV "1.1"                        // short Sketch version
#define MY_NODE_ID 1                    // (1-254) to manually set Node ID
/*
    Includes
=========1=========2=========3=========4=========5=========6=========7========*/
#include "R.h"                          // NRF24L01 definitions
#include <MySensors.h>                  // MySensors library
#include "def.h"                        // Explanation and inital variables
  #include "A1.h"                       // Relay for lights
  #include "A2.h"                       // Front Door Electronic Lock
  #include "S1.h"                       // Reed switch
  #include "S4.h"                       // PIR switch
/*
    Presentation
=========1=========2=========3=========4=========5=========6=========7========*/
void presentation(){ 
  sendSketchInfo(SN, SV);
    present(A1, S_BINARY, "Entryway Lights");
    present(A2, S_LOCK, "Entryway Lock");
    present(S1, S_DOOR, "Entryway Reed");
    present(S4, S_MOTION, "Entryway PIR");
  Serial.println((String)" === Node "+MY_NODE_ID+" presented ("+SN+")");
}
/*
    Setup
=========1=========2=========3=========4=========5=========6=========7========*/
void setup() {
    setupA1();
    setupA2();
    setupS1();
    setupS4();
  Serial.println((String)" === Node "+MY_NODE_ID+" setup ("+SN+")");
}
/*
    Loop
=========1=========2=========3=========4=========5=========6=========7========*/
void loop() {
    loopS1();
    loopS4();
  wait(1000);
}
/*
    Receive
=========1=========2=========3=========4=========5=========6=========7========*/
void receive(const MyMessage &message) {
    receiveA1(message);
    receiveA2(message);
}

// code stored in the sketch: NRF24L01.h
/* NRF24L01 defintions
=========1=========2=========3=========4=========5=========6=========7========*/
//#define MY_DEBUG                              // Enable debug prints to serial monitor
//#define MY_DEBUG_VERBOSE_RF24                 // Enable for verbose debug prints related to the RF24 driver. Requires DEBUG to be enabled.

#define MY_RADIO_NRF24                          // Enable if you want to use a NRF24L01+ radio
#define MY_REPEATER_FEATURE                     // Enables repeater functionality (relays messages from other nodes).

#define MY_RF24_PA_LEVEL RF24_PA_MAX            // Set radio power (Options are: _MIN, _LOW, _HIGH or _MAX)
#define MY_RF24_DATARATE RF24_250KBPS           // Set radio transmission rate

/* Optional & Additional
=========1=========2=========3=========4=========5=========6=========7========*/
//#define MY_RF24_CHANNEL 76                    // Change radio channel, has to be done on all nodes

//#define MY_SIGNING_ATSHA204                   // Enables hardware signing using ATSHA204
//#define MY_SIGNING_SOFT                       // Enables software signing

//#define MY_PARENT_NODE_ID                             
//#define MY_PARENT_NODE_IS_STATIC

//#define MY_DISABLED_SERIAL                    // Enable if you want to use TX(1), RX(0) as normal I/O pin
//#define MY_RF24_ENABLE_ENCRYPTION

// code stored in the sketch: R.h
/* 
    NRF24L01 defintions

=========1=========2=========3=========4=========5=========6=========7========*/
//#define MY_DEBUG                              // Enable debug prints to serial monitor
//#define MY_DEBUG_VERBOSE_RF24                 // Enable for verbose debug prints related to the RF24 driver. Requires DEBUG to be enabled.

#define MY_RADIO_NRF24                          // Enable if you want to use a NRF24L01+ radio
#define MY_REPEATER_FEATURE                     // Enables repeater functionality (relays messages from other nodes).

#define MY_RF24_PA_LEVEL RF24_PA_MAX            // Set radio power (Options are: _MIN, _LOW, _HIGH or _MAX)
#define MY_RF24_DATARATE RF24_250KBPS           // Set radio transmission rate

/* Optional & Additional
=========1=========2=========3=========4=========5=========6=========7========*/
//#define MY_RF24_CHANNEL 76                    // Change radio channel, has to be done on all nodes

//#define MY_SIGNING_ATSHA204                   // Enables hardware signing using ATSHA204
//#define MY_SIGNING_SOFT                       // Enables software signing

//#define MY_PARENT_NODE_ID                     // Gateway is 0
//#define MY_PARENT_NODE_IS_STATIC

//#define MY_DISABLED_SERIAL                    // Enable if you want to use TX(1), RX(0) as normal I/O pin
//#define MY_RF24_ENABLE_ENCRYPTION

// code stored in the sketch: s0.h
/* Passive InfraRed Switch
=========1=========2=========3=========4=========5=========6=========7========*/
MyMessage msg_s0(0, V_TRIPPED);        // define type of message sent to MySensors

/* Setup
=========1=========2=========3=========4=========5=========6=========7========*/
void setup_s0(){
    pinMode(pirPin, INPUT);            // initialize sensor as an input
}

/* Loop
=========1=========2=========3=========4=========5=========6=========7========*/
void loop_s0(){
    pirVal = digitalRead(pirPin);      // read and store sensor value
    wait(100);                	       // delay 100 milliseconds 

    if (pirVal == HIGH) {              // check if the sensor is tripped
        if (pirState == LOW) {         // change in status
//          Serial.println("Motion detected!");
            pirState = HIGH;       	   // update variable state to HIGH
            lightsOn();                // Switch on lights
        }
    } else {
        if (pirState == HIGH){         // change in status
//          Serial.println("Motion stopped!");
            pirState = LOW;       	   // update variable state to LOW
            lightsOff(5);              // Set timer to switch off light 5 minutes
        }
    }
}

// code stored in the sketch: S1.h
/* 
    Reed Switch

 - 	Since one end of the reed switch is connected to ground, 
	we need to pull-up the reed switch pin internally
 - 	Use Arduino’s internal pull-up resistor to bias the switch high
 - 	This effectively inverts the behavior of the INPUT mode, 
	where HIGH means the sensor is off, and LOW means the sensor is on.

*/

/*
    Initialize
=========1=========2=========3=========4=========5=========6=========7========*/
MyMessage msgS1(S1, V_TRIPPED);         // type of message sent to MySensors
/*
    Setup
=========1=========2=========3=========4=========5=========6=========7========*/
void setupS1(){
    pinMode(pinS1, INPUT_PULLUP);       // pull-up the pin internally !!!
}
/* 
    Loop
=========1=========2=========3=========4=========5=========6=========7========*/
void loopS1(){
    valueS1 = digitalRead(pinS1);       // Read the state of the switch
    if (valueS1 != stateS1) {           // If different from last state
        if (valueS1 == LOW){            // Pin reads low, the switch is closed
            Serial.println("S1 is Closed (Door Closed/Untripped)");
        } else {
            Serial.println("S1 is Open (Door Open/Tripped)");
        }
        send(msgS1.set(valueS1));       // send to controller
        stateS1 = valueS1;              // update state
    }
}
/*
    Receive
=========1=========2=========3=========4=========5=========6=========7========*/
// nothing to receive

// code stored in the sketch: s2.h
/* PhotoVoltaic Sensor
=========1=========2=========3=========4=========5=========6=========7========*/
MyMessage msg_s2(2, V_LIGHT);          // define type of message sent to MySensors

/* Setup
=========1=========2=========3=========4=========5=========6=========7========*/
void setup_s2(){
    pinMode(pvPin, INPUT);             // initialize sensor as an input
}

/* Loop
=========1=========2=========3=========4=========5=========6=========7========*/
void loop_s2(){
    pvVal = digitalRead(pvPin);   	   // read and store sensor value
    wait(100);             			       // delay 100 milliseconds 

    if (pvState != pvVal){             // if the state has changed
        pvState = pvVal;               // update state
        //  send message to mycontroller
    }
}

// code stored in the sketch: S3.h
/* 
    Passive InfraRed Switch

    - motion detector
    - once tripped should not react for the duration of a timer
    - if any new movement is detected, reset the timer
    
*/

/* Initialize
=========1=========2=========3=========4=========5=========6=========7========*/
MyMessage msgS3(S3, V_TRIPPED);        // define type of message sent to MySensors

/* Setup
=========1=========2=========3=========4=========5=========6=========7========*/
void setupS3(){
    pinMode(pinS3, INPUT);             // initialize sensor as an input
}

/* Loop
=========1=========2=========3=========4=========5=========6=========7========*/
void loopS3(){
    valueS3 = digitalRead(pinS3);       // read and store sensor value
    //Serial.print("PIR value is at: "); Serial.print(valueS3);
    //Serial.print(" -- PIR state is at: "); Serial.print(stateS3);
    //Serial.print(" -- PIR timer is at: "); Serial.println(timerS3);
    if (valueS3 == HIGH && stateS3 == LOW) {    // check if the sensor is tripped
        Serial.println("-----> Motion detected!");
        stateS3 = HIGH;       	                // update variable state to HIGH
        timerS3 ++;
//        lightsOn();                           // Switch on lights
    }
    if (stateS3 == HIGH){
        timerS3 ++;
    }
    if (timerS3>60){
        stateS3 = LOW;                           // update variable state to LOW
        timerS3=0;
//        lightsOff(5);                         // Set timer to switch off light 5 minutes
    }
    send(msgS3.set(valueS3 ? "1" : "0"));       // Send tripped value to gw
}

// code stored in the sketch: S4.h
/* 
    Passive InfraRed Switch
	
	
	
*/

/* Initialize
=========1=========2=========3=========4=========5=========6=========7========*/
MyMessage msgS4(S4, V_TRIPPED);        // type of message sent to MySensors

/* Setup
=========1=========2=========3=========4=========5=========6=========7========*/
void setupS4(){
    pinMode(pinS4, INPUT);             // initialize sensor as an input
	stateS4 = request(S4, V_TRIPPED);  // get status from controller
    digitalWrite(pinS4, stateS4);      // turn on/off based on controller state

}

/* Loop
=========1=========2=========3=========4=========5=========6=========7========*/
void loopS4(){
	valueS4 = digitalRead(pinS4);       // Read the state of the switch
	if (valueS4 != stateS4) {           // If different from last state
        if (valueS4 == 0){              // Pin reads low, the door is closed.
			Serial.println((String)"- Standing down after "+ ((millis()-tS4)/1000) + " seconds");
        } else if (valueS4 == 1){
			tS4 = millis();				// time when loop fired (for calibrating the timer)
			Serial.println("--- Motion detected! --- ");
        }
        send(msgS4.set(valueS4));       // send to controller
        stateS4 = valueS4;              // update state
		wait(2000);						// wait 2 seconds so it doesnt bounce
    }
}

// code stored in the sketch: S5.h
/*
    Reed Switch

    - checks if door is open or sut
*/

/* Initialize
=========1=========2=========3=========4=========5=========6=========7========*/
MyMessage msgS5(S5, V_TRIPPED);        // define type of message sent to MySensors

/* Setup
=========1=========2=========3=========4=========5=========6=========7========*/
void setupS5(){
    pinMode(pinS5, INPUT);             // initialize sensor as an input
}

/* Loop
=========1=========2=========3=========4=========5=========6=========7========*/
void loopS5(){
    valueS5 = digitalRead(pinS5);      // read and store sensor value
    if (valueS5 == HIGH) {             // check if the sensor is tripped
        //Serial.println("Your Door is Closed");
    } else {
        //Serial.println("Your Door is Open");
    }
    send(msgS5.set(valueS5 ? "0" : "1"));       // Send tripped value to gw
}

// code stored in the sketch: xxx.h
/*
    FRONT DOOR

    RADIO
repeater

    SENSORS
PIR switch - to check if someone is in front of the door
Reed switch - to sense if door is open or closed
Photovoltaic sensor -  to check if it's day or night
? Electric lock - status if door is locked

    ACTUATORS
Relay, to switch on the lights
? Lock/Unlock via electrick lock

*/

// code stored in the sketch: zzz.h

/*       ACTUATORS
=========1=========2=========3=========4=========5=========6=========7========*/

//  Relay for lights
#define A1 1                            // Sensor number
const int pinA1 = 2;                    // the pin that the relay is atteched to

//  Lock/Unlock front door via electrick lock
#define A2 2                            // Sensor number
const int pinA2_lock = 3;               // the pin that locks the door
const int pinA2_unlock = 4;             // the pin that unlockes the door
int stateA2 = 0;                        // by default, the door is locked


/*       SENSORS
=========1=========2=========3=========4=========5=========6=========7========*/

//  Reed switch - to sense if the door is open or closed
#define S1 3                            // Sensor number
const int pinS1 = 5;                    // the pin that the reed switch is atteched to
int valueS1 = 0;                        // variable for reading the sensor status
int stateS1 = 0;                        // variable for storing the last state

//  PIR switch - to check if someone is in front of the door
#define S4 4                            // Sensor number
const int pinS4 = 6;                    // data pin
int valueS4 = 0;                        // variable for reading the sensor status
int stateS4 = 0;                        // variable for storing the last state
unsigned long startS4;
